# Fritzing sketch AndroBot_Arm (saved by Fritzing 0.9.3b)
perfboards: 1

parts:
  Part1 = Arduino Uno (Rev3)
  J1 = Basic Servo
  J2 = Basic Servo
  J3 = Basic Servo
  J4 = Basic Servo
  Power_plug1 = Power plug  # not connected
  Part2 = Bluetooth HC-05 Macho  # not connected

nets:
  N1: Part1.D9_PWM, J4.pulse
  N2: Part1.D3_PWM, J3.pulse
  N3: Part1.D5_PWM, J2.pulse
  N4: Part1.D6_PWM, J1.pulse
  5V: Part1.5V, J2.vcc
  GND: Part1.GND, J2.gnd, J4.gnd
